// Logisim project 5-bitALU.circ as structural Verilog: 1 circuit, main circuit main
module main (
);

  wire A0, A1, A2, A3, A4, B0, B1, B2, B3, B4, C0, C0P0_out, C1, C1P1_out, C2, C2P2_out, C3, C3P3_out, C4,
       C4P4_out, C5, CIN, clock_1_out, clock_2_out, G0_out, G1_out, G2_out, G3_out, G4_out, go, HCLK,
       not_2_out, P0_out, P1_out, P2_out, P3_out, P4_out, reset, S0, S1;
  wire [2:0] multiplexer_2_out;
  wire [3:0] or_1_out;
  wire [4:0] and_1_out, not_1_out, or_6_out;
  wire [6:1] counter_1_q;

  xor P0 (P0_out, A0, B0);
  and G0 (G0_out, A0, B0);
  xor P1 (P1_out, A1, B1);
  and G1 (G1_out, A1, B1);
  xor P2 (P2_out, A2, B2);
  and G2 (G2_out, A2, B2);
  xor P3 (P3_out, A3, B3);
  and G3 (G3_out, A3, B3);
  xor P4 (P4_out, A4, B4);
  and G4 (G4_out, A4, B4);
  and C0P0 (C0P0_out, P0_out, CIN);
  and C1P1 (C1P1_out, P1_out, or_1_out[0]);
  and C2P2 (C2P2_out, P2_out, or_1_out[1]);
  and C3P3 (C3P3_out, P3_out, or_1_out[2]);
  and C4P4 (C4P4_out, P4_out, or_1_out[3]);
  or or_1 (or_1_out[0], C0P0_out, G0_out);
  or or_2 (or_1_out[1], C1P1_out, G1_out);
  or or_3 (or_1_out[2], C2P2_out, G2_out);
  or or_4 (or_1_out[3], C3P3_out, G3_out);
  or or_5 (C5, C4P4_out, G4_out);
  assign not_1_out = ~{A4, A3, A2, A1, A0};  // NOT_Gate not_1, 5 bits wide
  assign and_1_out = {B3, B4, B2, B1, B0} & {A4, A3, A2, A1, A0};  // AND_Gate and_1, 5 bits wide
  assign or_6_out = {A4, A3, A2, A1, A0} | {B3, B4, B2, B1, B0};  // OR_Gate or_6, 5 bits wide
  Multiplexer #(.select(2), .width(5)) multiplexer_1 (
    .in0(and_1_out), .in1(or_6_out), .in2(not_1_out), .in3({C5, or_1_out}), .out({C4, C3, C2, C1, C0}),
    .sel({S1, S0}));  // open: en
  // Probe on {C5, C4, C3}
  // Probe on {C2, C1, C0}
  // Probe on multiplexer_2_out
  // Probe on {4'b0110, multiplexer_2_out}
  Multiplexer #(.width(3)) multiplexer_2 (
    .in0({C5, C4, C3}), .in1({C2, C1, C0}), .out(multiplexer_2_out), .sel(HCLK));  // open: en
  TTY #(.rows(32), .cols(2)) tty_1 (.data({4'b0110, multiplexer_2_out}), .clk(clock_1_out), .we(go), .clr(reset));
  Clock clock_1 (.out(clock_1_out));
  // Probe on {A4, A3, A2, A1, A0, CIN}
  // Probe on {B4, B3, B2, B1, B0}
  // Probe on S1
  Clock clock_2 (.out(clock_2_out));
  // Probe on S0
  not not_2 (not_2_out, HCLK);
  Counter #(.width(7), .max('h7f), .ongoal("stay")) counter_1 (
    .Q({counter_1_q, HCLK}), .clk(clock_2_out), .clr(reset));  // open: load, D, count, carry
  Button u_Reset (.out(reset));
  Random #(.width(13), .seed(34573)) random_1 (
    .clk(not_2_out), .next(go), .out({B4, B3, B2, B1, B0, A4, A3, A2, A1, A0, CIN, S1, S0}), .clr(reset));
  not not_3 (go, counter_1_q[6]);

  // Notes on the sheet:
  //   ADD
  //   cout
  //   ~A
  //   A AND B
  //   A OR B
  //   Fed into Mux with selector bits
  //   outputs
  //   07
  //   51
  //   40
  //   51
  //   77
  //   77
  //   57
  //   63
  //   43
  //   77
  //   60
  //   51
  //   46
  //   71
  //   32
  //   43
  //   34
  //   50
  //   53
  //   00
  //   07
  //   02
  //   74
  //   04
  //   35
  //   52
  //   52
  //   50
  //   65
  //   46
  //   11
  //   57
endmodule
