// Logisim project BCD-to-7.circ as structural Verilog: 1 circuit, main circuit main
module main (
);

  wire a, and_1_out, and_2_out, and_3_out, and_4_out, b, B_nC_2_out, B_nC_out, B_nCD_out, B_nD_out, c,
       C_nD_2_out, C_nD_3_out, C_nD_out, d, e, f, g, nB_nD_2_out, nB_nD_out, nBC_2_out, nBC_out, nC_nD_out,
       not_1_out, not_2_out, not_3_out, not_4_out, not_5_out, not_6_out, not_7_out, not_8_out, not_9_out,
       not_10_out, not_11_out, not_12_out, not_13_out, not_14_out, not_15_out, not_16_out, w0, w1, w2, w3;

  not not_1 (not_1_out, w2);
  not not_2 (not_2_out, w0);
  not not_3 (not_3_out, w2);
  not not_4 (not_4_out, w1);
  not not_5 (not_5_out, w0);
  not not_6 (not_6_out, w1);
  not not_7 (not_7_out, w2);
  not not_8 (not_8_out, w1);
  not not_9 (not_9_out, w0);
  not not_10 (not_10_out, w2);
  not not_11 (not_11_out, w0);
  not not_12 (not_12_out, w1);
  not not_13 (not_13_out, w0);
  not not_14 (not_14_out, w2);
  not not_15 (not_15_out, w1);
  not not_16 (not_16_out, w0);
  and and_1 (and_1_out, not_1_out, not_2_out);
  and and_2 (and_2_out, w2, w0);
  and and_3 (and_3_out, not_4_out, not_5_out);
  and and_4 (and_4_out, w1, w0);
  and nB_nD (nB_nD_out, not_7_out, not_9_out);
  and nBC (nBC_out, not_7_out, w1);
  and C_nD (C_nD_out, w1, not_9_out);
  and B_nCD (B_nCD_out, w2, not_8_out, w0);
  and nB_nD_2 (nB_nD_2_out, not_10_out, not_11_out);
  and C_nD_2 (C_nD_2_out, w1, not_11_out);
  and nC_nD (nC_nD_out, not_12_out, not_13_out);
  and B_nC (B_nC_out, w2, not_12_out);
  and B_nD (B_nD_out, w2, not_13_out);
  and nBC_2 (nBC_2_out, not_14_out, w1);
  and C_nD_3 (C_nD_3_out, w1, not_16_out);
  and B_nC_2 (B_nC_2_out, w2, not_15_out);
  or or_1 (c, w2, not_6_out, w0);
  or or_2 (d, w3, nB_nD_out, nBC_out, C_nD_out, B_nCD_out);
  or or_3 (e, nB_nD_2_out, C_nD_2_out);
  or or_4 (f, w3, nC_nD_out, B_nC_out, B_nD_out);
  or or_5 (g, w3, nBC_2_out, C_nD_3_out, B_nC_2_out);
  or or_6 (a, w3, and_1_out, w1, and_2_out);
  or or_7 (b, not_3_out, and_3_out, and_4_out);

  // Notes on the sheet:
  //   A
  //   B
  //   C
  //   D
  //   A
  //   B
  //   C
  //   D
  //   A
  //   B
  //   C
  //   D
  //   A
  //   B
  //   C
  //   D
  //   A
  //   B
  //   C
  //   D
  //   A
  //   B
  //   C
  //   D
  //   A
  //   B
  //   C
  //   D
  //   bcd.circ (a)
  //   ~B
  //   ~D
  //   bcd.circ (b)
  //   ~B
  //   ~C
  //   ~D
  //   bcd.circ (c)
  //   ~C
  //   ~B
  //   ~C
  //   ~D
  //   ~B
  //   ~D
  //   bcd.circ (f)
  //   ~C
  //   ~D
  //   ~B
  //   ~C
  //   ~D
  //   (~B~D)
  //   (BD)
  //   (~C~D)
  //   (CD)
  //   bcd.circ (d)
  //   bcd.circ (e)
  //   bcd.circ (g)
  //   a = A+C+(~B~D)+(BD)
  //   b =~B+(~C~D)+(CD)
  //   c = B+~C+D
  //   e = (~B~D)+(C~D)
  //   g = A+(~BC)+(C~D)+(B~C)
  //   d = A+(~B~D)+(~BC)+(C~D)+(B~CD)
  //   f = A+(~C~D)+(B~C)+(B~D)
endmodule
