// Logisim project CPU.circ as structural Verilog: 5 circuits, main circuit main
// CLA
module main (
  output [9:0] out_1,
  output [9:0] out_2,
  output [9:0] out_3,
  output [9:0] out_4,
  output [9:0] out_5,
  output [9:0] out_6,
  output [9:0] out_7,
  output [9:0] out_8,
  output [9:0] out_9,
  output [9:0] out_10,
  output [9:0] out_11,
  output [9:0] out_12,
  output ignore,
  output [9:0] out_14,
  output halt,
  output [9:0] out_16,
  output [9:0] out_17,
  output [4:0] out_18
);

  wire and_1_out, CLK, clock_1_out, comparator_1_lt, comparator_2_lt, d_ff_1_q, d_ff_3_qn, d_ff_4_qn,
       d_ff_5_qn, d_ff_6_qn, d_ff_7_qn, decoder_1_out7, HALT_t, nop, not_1_out, not_2_out, Reset, STOP,
       t_ff_2_q, TClock;
  wire [1:0] counter_2_q, Upper_2_bits;
  wire [2:0] Mux_A, Mux_B, Reg_Select, rom_1_data;
  wire [4:0] _5_bit_up_counter, counter_1_q, opcode_t;
  wire [6:0] adder_1_out, adder_2_out, ASCII, decoder_1_out0, LSB, MiddleBits;
  wire [7:0] multiplexer_4_out;
  wire [9:0] Data, multiplexer_2_out, multiplexer_3_out;

  not not_1 (not_1_out, STOP);
  Decoder #(.select(3)) decoder_1 (
    .out0(decoder_1_out0[0]), .out1(decoder_1_out0[1]), .out2(decoder_1_out0[2]), .out3(decoder_1_out0[3]),
    .out4(decoder_1_out0[4]), .out5(decoder_1_out0[5]), .out6(decoder_1_out0[6]), .out7(decoder_1_out7),
    .sel(Reg_Select), .en(not_1_out));
  // Probe on decoder_1_out0
  RAM #(.addrWidth(5), .dataWidth(24)) ram_1 (
    .addr(_5_bit_up_counter), .data({out_18, Reg_Select, Mux_A, Mux_B, Data}), .clk(CLK), .clr(STOP));  // open: sel, ld
  D_Flip_Flop d_ff_1 (.clk(CLK), .D(HALT_t), .Q(d_ff_1_q));  // open: Qn, preset, en, reset
  Multiplexer #(.select(5), .enable("false")) multiplexer_1 (
    .in0(1'b0), .in1(1'b0), .in2(1'b0), .in3(1'b0), .in4(1'b0), .in5(1'b0), .in6(1'b0), .in7(1'b0),
    .in8(1'b0), .in9(1'b0), .in10(1'b0), .in11(1'b0), .in15(1'b1), .out(HALT_t), .sel(opcode_t));  // open: in12, in13, in14, in16, in17, in18, in19, in20, in21, in22, in23, in24, in25, in26, in27, in28, in29, in30, in31
  Register_Bank register_bank_1 (
    .Decoder_s_Output(decoder_1_out0), .Data(out_7), .T_Clock(CLK), .out_5(out_1), .out_6(out_3),
    .out_7(out_5), .out_8(out_6), .out_9(out_9), .out_10(out_10), .out_11(out_12));  // open: Reset
  D_Flip_Flop d_ff_2 (.clk(d_ff_1_q), .D(d_ff_1_q), .Q(STOP));  // open: Qn, preset, en, reset
  Multiplexer #(.select(3), .width(10)) multiplexer_2 (
    .in0(out_1), .in1(out_3), .in2(out_5), .in3(out_6), .in4(out_9), .in5(out_10), .in6(out_12),
    .out(multiplexer_2_out), .sel(Mux_A));  // open: in7, en
  ALU alu_1 (
    .Output(out_7), .OpCode(out_18), .halt(HALT_t), .nop(nop), .in_1(multiplexer_2_out),
    .in_2(multiplexer_3_out), .Instruction_Data(Data));
  TTY #(.rows(33), .cols(4)) tty_1 (.data(ASCII), .clk(TClock));  // open: we, clr
  Multiplexer #(.select(3), .width(10)) multiplexer_3 (
    .in0(out_1), .in1(out_3), .in2(out_5), .in3(out_6), .in4(out_9), .in5(out_10), .in6(out_12), .in7(Data),
    .out(multiplexer_3_out), .sel(Mux_B));  // open: en
  // Probe on out_1
  // Probe on out_9
  Counter #(.width(5), .max('h1f), .ongoal("stay")) counter_1 (
    .Q(counter_1_q), .carry(halt), .clk(CLK));  // open: load, D, count, clr
  // Probe on out_3
  // Probe on out_10
  Multiplexer #(.select(3), .width(10)) multiplexer_4 (
    .in0(out_1), .in1(out_3), .in2(out_5), .in3(out_6), .in4(out_9), .in5(out_10), .in6(out_12),
    .out({Upper_2_bits, multiplexer_4_out}), .sel(rom_1_data));  // open: in7, en
  not not_2 (not_2_out, halt);
  Clock clock_1 (.out(clock_1_out));
  ROM #(.addrWidth(5), .dataWidth(3)) rom_1 (.addr(counter_1_q), .data(rom_1_data));  // open: sel
  and and_1 (and_1_out, not_2_out, clock_1_out);
  not not_3 (TClock, and_1_out);
  // Probe on out_5
  // Probe on out_12
  D_Flip_Flop d_ff_3 (
    .clk(CLK), .D(d_ff_3_qn), .Q(_5_bit_up_counter[0]), .Qn(d_ff_3_qn), .reset(Reset));  // open: preset, en
  // Probe on out_6
  Comparator #(.width(7)) comparator_1 (
    .a(7'b0111001), .b({3'b011, multiplexer_4_out[3:0]}), .lt(comparator_1_lt));  // open: gt, eq
  Comparator #(.width(7)) comparator_2 (
    .a(7'b0111001), .b({3'b011, multiplexer_4_out[7:4]}), .lt(comparator_2_lt));  // open: gt, eq
  T_Flip_Flop t_ff_1 (.clk(t_ff_2_q), .T(1'b1), .Q(CLK));  // open: Qn, preset, reset, en
  T_Flip_Flop t_ff_2 (.clk(and_1_out), .T(1'b1), .Q(t_ff_2_q));  // open: Qn, preset, reset, en
  Adder #(.width(7)) adder_1 (
    .a({3'b011, multiplexer_4_out[3:0]}), .b(7'b0000111), .out(adder_1_out));  // open: cin, cout
  Adder #(.width(7)) adder_2 (
    .a({3'b011, multiplexer_4_out[7:4]}), .b(7'b0000111), .out(adder_2_out));  // open: cin, cout
  Multiplexer #(.select(2), .width(7)) multiplexer_5 (
    .in0({5'b01100, Upper_2_bits}), .in1(MiddleBits), .in2(LSB), .in3(7'b0100000), .out(ASCII),
    .sel(counter_2_q));  // open: en
  Counter #(.width(2), .max('h3)) counter_2 (.Q(counter_2_q), .clk(TClock));  // open: load, D, count, carry, clr
  D_Flip_Flop d_ff_4 (
    .clk(d_ff_3_qn), .D(d_ff_4_qn), .Q(_5_bit_up_counter[1]), .Qn(d_ff_4_qn), .reset(Reset));  // open: preset, en
  Multiplexer #(.width(7), .disabled(0), .enable("false")) multiplexer_6 (
    .in0({3'b011, multiplexer_4_out[3:0]}), .in1(adder_1_out), .out(LSB), .sel(comparator_1_lt));
  Multiplexer #(.width(7), .disabled(0), .enable("false")) multiplexer_7 (
    .in0({3'b011, multiplexer_4_out[7:4]}), .in1(adder_2_out), .out(MiddleBits), .sel(comparator_2_lt));
  D_Flip_Flop d_ff_5 (
    .clk(d_ff_4_qn), .D(d_ff_5_qn), .Q(_5_bit_up_counter[2]), .Qn(d_ff_5_qn), .reset(Reset));  // open: preset, en
  D_Flip_Flop d_ff_6 (
    .clk(d_ff_5_qn), .D(d_ff_6_qn), .Q(_5_bit_up_counter[3]), .Qn(d_ff_6_qn), .reset(Reset));  // open: preset, en
  T_Flip_Flop t_ff_3 (.clk(CLK), .T(1'b1), .Q(ignore));  // open: Qn, preset, reset, en
  D_Flip_Flop d_ff_7 (
    .clk(d_ff_6_qn), .D(d_ff_7_qn), .Q(_5_bit_up_counter[4]), .Qn(d_ff_7_qn), .reset(Reset));  // open: preset, en

  assign out_2 = out_1;
  assign out_4 = out_3;
  assign out_8 = out_5;
  assign out_11 = out_6;
  assign out_14 = out_9;
  assign out_16 = out_10;
  assign out_17 = out_12;

  // Other names for the same wires on the sheet: OpCode[4:0] = out_18; ALU_out[9:0] = out_7; R0[9:0] = out_1;
  //   R1[9:0] = out_3; R2[9:0] = out_5; R3[9:0] = out_6; R4[9:0] = out_9; R5[9:0] = out_10; R6[9:0] = out_12

  // Notes on the sheet:
  //   Matthew Moua
  //   999198117
  //   DO NOT PUT ANY PINS ON THE main circuit.  (You should not need any anyway.)
  //   20:BNEZ
  //   0F5
  //   0F5
  //   25A
  //   050
  //   2FF
  //   30A
  //   34F
  //   0F5
  //   1EA
  //   07A
  //   29B
  //   165
  //   10F
  //   0F5
  //   0AA
  //   0AA
  //   05A
  //   00A
  //   0FA
  //   104
  //   0B4
  //   165
  //   165
  //   001
  //   001
  //   000
  //   000
  //   000
  //   000
  //   000
  //   ???
  //   There is no Reset.  Just Ctrl-r, then load test.txt into your RAM, and then Ctrl-k
  //   You must  use the CLK tunnel for the source of your clock.  R0-R6 are the other tunnels you need to connect
  //   contents of rom_1 (hex, n*v repeats v):
  //   0 0 0 1 2 3 4 5 6 2 3 4 5 6 0 0 0 1 3 4 6 3 5 5 8*6
endmodule

module CLA (
  input  in_1,
  input  in_2,
  input  in_3,
  input  in_4,
  input  in_5,
  input  in_6,
  input  in_7,
  input  in_8,
  input  in_9,
  input  in_10,
  input  in_11,
  output out_12,
  output out_13,
  output out_14,
  output out_15,
  output out_16,
  output out_17
);

  wire and_1_out, and_2_out, and_3_out, and_4_out, and_5_out, and_6_out, and_7_out, and_8_out, and_9_out,
       and_10_out, and_11_out, and_12_out, C0P0_out, c1, c2, c3, c4, CP0P1_out, G0_out, G0P1_out, G1_out,
       G2_out, G3_out, G4_out, P0_out, P1_out, P2_out, P3_out, P4_out;

  xor P0 (P0_out, in_1, in_6);
  and G0 (G0_out, in_6, in_1);
  and C0P0 (C0P0_out, P0_out, in_11);
  or or_1 (c1, G0_out, C0P0_out);
  xor xor_1 (out_12, P0_out, in_11);
  and G1 (G1_out, in_7, in_2);
  xor P1 (P1_out, in_2, in_7);
  and G0P1 (G0P1_out, P1_out, G0_out);
  and CP0P1 (CP0P1_out, P1_out, P0_out, in_11);
  or or_2 (c2, G1_out, CP0P1_out, G0P1_out);
  xor xor_2 (out_13, P1_out, c1);
  xor P2 (P2_out, in_3, in_8);
  and G2 (G2_out, in_8, in_3);
  xor xor_3 (out_14, P2_out, c2);
  and and_1 (and_1_out, P2_out, P0_out, in_11, P1_out);
  and and_2 (and_2_out, G1_out, P2_out);
  or or_3 (c3, G2_out, and_1_out, and_2_out, and_3_out);
  and and_3 (and_3_out, P2_out, P1_out, G0_out);
  xor P3 (P3_out, in_4, in_9);
  and G3 (G3_out, in_9, in_4);
  and and_4 (and_4_out, P2_out, P3_out, G1_out);
  and and_5 (and_5_out, P3_out, G2_out);
  xor xor_4 (out_15, P3_out, c3);
  and and_6 (and_6_out, P3_out, P2_out, P1_out, G0_out);
  or or_4 (c4, G3_out, and_5_out, and_4_out, and_6_out, and_7_out);
  and and_7 (and_7_out, P3_out, P2_out, P1_out, P0_out, in_11);
  xor P4 (P4_out, in_5, in_10);
  and G4 (G4_out, in_10, in_5);
  and and_8 (and_8_out, P4_out, P3_out, G2_out);
  and and_9 (and_9_out, P4_out, G3_out);
  xor xor_5 (out_16, P4_out, c4);
  and and_10 (and_10_out, P4_out, P3_out, P2_out, G1_out);
  or or_5 (out_17, and_9_out, and_8_out, and_10_out, G4_out, and_11_out, and_12_out);
  and and_11 (and_11_out, P4_out, P3_out, P2_out, P1_out, G0_out);
  and and_12 (and_12_out, P4_out, P3_out, P2_out, P1_out, P0_out, in_11);

  // Notes on the sheet:
  //   ALU RECREATED
endmodule

module ALU (
  input  [9:0] in_1,
  input  [9:0] in_2,
  input  [9:0] Instruction_Data,
  input  [4:0] OpCode,
  output [9:0] Output,
  output halt,
  output nop
);

  wire cla_1_out_17, cla_2_out_17, multiplexer_1_out, multiplexer_2_out, multiplexer_4_out,
       multiplexer_5_out, multiplexer_6_out, multiplexer_7_out, multiplexer_8_out, multiplexer_9_out,
       multiplexer_11_out, multiplexer_12_out, multiplexer_13_out, multiplexer_14_out, multiplexer_16_out,
       multiplexer_17_out, multiplexer_18_out, multiplexer_19_out, multiplexer_20_out, multiplexer_21_out,
       multiplexer_22_out, multiplexer_23_out, not_2_out, not_3_out, not_4_out, not_5_out, not_6_out,
       not_7_out, not_8_out, not_9_out, not_10_out, not_11_out, not_12_out, not_13_out, not_14_out,
       not_15_out, not_17_out, not_18_out, not_19_out, not_20_out, not_21_out, not_22_out, S0, S1, S2, S3,
       S4, S5, S6, S7, S8, S9, Si0, Si1, Si2, Si3, Si4, Si5, Si6, Si7, Si8, Si9;
  wire [9:0] _000, ADD, ADDI, AND, BNEZ, HALT_t, NOT, not_16_out, OR, SLL, SRL, SUB, SUBI;

  assign AND = in_1 & in_2;  // AND_Gate and_1, 10 bits wide
  assign OR = in_1 | in_2;  // OR_Gate or_1, 10 bits wide
  assign NOT = ~in_1;  // NOT_Gate not_1, 10 bits wide
  Shifter #(.width(10)) shifter_1 (.in(in_1), .\dist (4'b0001), .out(SLL));
  Shifter #(.width(10), .shift("lr")) shifter_2 (.in(in_1), .\dist (4'b0001), .out(SRL));
  Adder #(.width(10)) adder_1 (.a(in_1), .b(in_2), .out(ADD));  // open: cin, cout
  Subtractor #(.width(10)) subtractor_1 (.a(in_1), .b(in_2), .out(SUB));  // open: bin, bout
  Adder #(.width(10)) adder_2 (.a(in_1), .b(Instruction_Data), .out(ADDI));  // open: cin, cout
  not not_2 (not_2_out, in_2[0]);
  Multiplexer #(.enable("false")) multiplexer_1 (
    .in0(in_2[0]), .in1(not_2_out), .out(multiplexer_1_out), .sel(OpCode[4]));
  CLA cla_1 (
    .in_1(in_1[0]), .in_2(in_1[1]), .in_3(in_1[2]), .in_6(multiplexer_1_out), .in_7(multiplexer_4_out),
    .in_8(multiplexer_7_out), .in_11(OpCode[4]), .out_12(S0), .out_13(S1), .out_14(S2), .in_4(in_1[3]),
    .in_5(in_1[4]), .out_15(S3), .out_16(S4), .in_9(multiplexer_8_out), .in_10(multiplexer_11_out),
    .out_17(cla_1_out_17));
  not not_3 (not_3_out, Instruction_Data[0]);
  Multiplexer #(.enable("false")) multiplexer_2 (
    .in0(Instruction_Data[0]), .in1(not_3_out), .out(multiplexer_2_out), .sel(OpCode[3]));
  CLA cla_2 (
    .in_1(in_1[0]), .in_2(in_1[1]), .in_3(in_1[2]), .in_6(multiplexer_2_out), .in_7(multiplexer_5_out),
    .in_8(multiplexer_6_out), .in_11(OpCode[3]), .out_12(Si0), .out_13(Si1), .out_14(Si2), .in_4(in_1[3]),
    .in_5(in_1[4]), .out_15(Si3), .out_16(Si4), .in_9(multiplexer_9_out), .in_10(multiplexer_12_out),
    .out_17(cla_2_out_17));
  assign BNEZ = in_1 | Instruction_Data;  // OR_Gate or_2, 10 bits wide
  Subtractor #(.width(10)) subtractor_2 (.a(in_1), .b(Instruction_Data), .out(SUBI));  // open: bin, bout
  Multiplexer #(.select(5), .enable("false")) multiplexer_3 (
    .in0(1'b0), .in1(1'b0), .in2(1'b0), .in3(1'b0), .in4(1'b0), .in5(1'b0), .in6(1'b0), .in7(1'b0),
    .in8(1'b0), .in9(1'b0), .in10(1'b0), .in11(1'b0), .in15(1'b1), .out(halt), .sel(OpCode));  // open: in12, in13, in14, in16, in17, in18, in19, in20, in21, in22, in23, in24, in25, in26, in27, in28, in29, in30, in31
  not not_4 (not_4_out, in_2[1]);
  Multiplexer #(.enable("false")) multiplexer_4 (
    .in0(in_2[1]), .in1(not_4_out), .out(multiplexer_4_out), .sel(OpCode[4]));
  not not_5 (not_5_out, Instruction_Data[1]);
  not not_6 (not_6_out, Instruction_Data[2]);
  Multiplexer #(.enable("false")) multiplexer_5 (
    .in0(Instruction_Data[1]), .in1(not_5_out), .out(multiplexer_5_out), .sel(OpCode[3]));
  Multiplexer #(.enable("false")) multiplexer_6 (
    .in0(Instruction_Data[2]), .in1(not_6_out), .out(multiplexer_6_out), .sel(OpCode[3]));
  not not_7 (not_7_out, in_2[2]);
  Multiplexer #(.enable("false")) multiplexer_7 (
    .in0(in_2[2]), .in1(not_7_out), .out(multiplexer_7_out), .sel(OpCode[4]));
  not not_8 (not_8_out, in_2[3]);
  Multiplexer #(.enable("false")) multiplexer_8 (
    .in0(in_2[3]), .in1(not_8_out), .out(multiplexer_8_out), .sel(OpCode[4]));
  not not_9 (not_9_out, Instruction_Data[3]);
  Multiplexer #(.enable("false")) multiplexer_9 (
    .in0(Instruction_Data[3]), .in1(not_9_out), .out(multiplexer_9_out), .sel(OpCode[3]));
  Multiplexer #(.select(5), .enable("false")) multiplexer_10 (
    .in0(1'b0), .in1(1'b0), .in2(1'b0), .in3(1'b0), .in4(1'b0), .in5(1'b0), .in6(1'b0), .in7(1'b0),
    .in8(1'b0), .in9(1'b0), .in10(1'b0), .in11(1'b1), .out(nop), .sel(OpCode));  // open: in12, in13, in14, in15, in16, in17, in18, in19, in20, in21, in22, in23, in24, in25, in26, in27, in28, in29, in30, in31
  not not_10 (not_10_out, in_2[4]);
  Multiplexer #(.enable("false")) multiplexer_11 (
    .in0(in_2[4]), .in1(not_10_out), .out(multiplexer_11_out), .sel(OpCode[4]));
  not not_11 (not_11_out, Instruction_Data[4]);
  Multiplexer #(.enable("false")) multiplexer_12 (
    .in0(Instruction_Data[4]), .in1(not_11_out), .out(multiplexer_12_out), .sel(OpCode[3]));
  not not_12 (not_12_out, in_2[5]);
  Multiplexer #(.enable("false")) multiplexer_13 (
    .in0(in_2[5]), .in1(not_12_out), .out(multiplexer_13_out), .sel(OpCode[4]));
  CLA cla_3 (
    .in_1(in_1[5]), .in_2(in_1[6]), .in_3(in_1[7]), .in_6(multiplexer_13_out), .in_7(multiplexer_16_out),
    .in_8(multiplexer_19_out), .in_11(cla_1_out_17), .out_12(S5), .out_13(S6), .out_14(S7), .in_4(in_1[8]),
    .in_5(in_1[9]), .out_15(S8), .out_16(S9), .in_9(multiplexer_21_out), .in_10(multiplexer_22_out));  // open: out_17
  not not_13 (not_13_out, Instruction_Data[5]);
  Multiplexer #(.enable("false")) multiplexer_14 (
    .in0(Instruction_Data[5]), .in1(not_13_out), .out(multiplexer_14_out), .sel(OpCode[3]));
  CLA cla_4 (
    .in_1(in_1[5]), .in_2(in_1[6]), .in_3(in_1[7]), .in_6(multiplexer_14_out), .in_7(multiplexer_17_out),
    .in_8(multiplexer_18_out), .in_11(cla_2_out_17), .out_12(Si5), .out_13(Si6), .out_14(Si7),
    .in_4(in_1[8]), .in_5(in_1[9]), .out_15(Si8), .out_16(Si9), .in_9(multiplexer_20_out),
    .in_10(multiplexer_23_out));  // open: out_17
  Multiplexer #(.select(5), .width(10), .enable("false")) multiplexer_15 (
    .in0(AND), .in1(OR), .in2(NOT), .in3(ADD), .in4(in_1), .in5(SLL), .in6(SRL), .in7(SUB), .in8(ADDI),
    .in9(SUBI), .in10(Instruction_Data), .in11(_000), .in12(SUBI), .in17(SUB), .in18(ADD), .in19(SLL),
    .in20(BNEZ), .in21(Instruction_Data), .in22(Instruction_Data), .in23(SUBI), .in24(in_1), .in25(BNEZ),
    .in26(HALT_t), .in27(Instruction_Data), .out(Output), .sel(OpCode));  // open: in13, in14, in15, in16, in28, in29, in30, in31
  not not_14 (not_14_out, in_2[6]);
  Multiplexer #(.enable("false")) multiplexer_16 (
    .in0(in_2[6]), .in1(not_14_out), .out(multiplexer_16_out), .sel(OpCode[4]));
  not not_15 (not_15_out, Instruction_Data[6]);
  Multiplexer #(.enable("false")) multiplexer_17 (
    .in0(Instruction_Data[6]), .in1(not_15_out), .out(multiplexer_17_out), .sel(OpCode[3]));
  Multiplexer #(.enable("false")) multiplexer_18 (
    .in0(Instruction_Data[7]), .in1(not_19_out), .out(multiplexer_18_out), .sel(OpCode[3]));
  assign _000 = in_1 & not_16_out;  // AND_Gate and_2, 10 bits wide
  assign not_16_out = ~in_1;  // NOT_Gate not_16, 10 bits wide
  not not_17 (not_17_out, in_2[7]);
  Multiplexer #(.enable("false")) multiplexer_19 (
    .in0(in_2[7]), .in1(not_17_out), .out(multiplexer_19_out), .sel(OpCode[4]));
  not not_18 (not_18_out, Instruction_Data[8]);
  not not_19 (not_19_out, Instruction_Data[7]);
  Multiplexer #(.enable("false")) multiplexer_20 (
    .in0(Instruction_Data[8]), .in1(not_18_out), .out(multiplexer_20_out), .sel(OpCode[3]));
  not not_20 (not_20_out, in_2[8]);
  Multiplexer #(.enable("false")) multiplexer_21 (
    .in0(in_2[8]), .in1(not_20_out), .out(multiplexer_21_out), .sel(OpCode[4]));
  not not_21 (not_21_out, in_2[9]);
  Multiplexer #(.enable("false")) multiplexer_22 (
    .in0(in_2[9]), .in1(not_21_out), .out(multiplexer_22_out), .sel(OpCode[4]));
  not not_22 (not_22_out, Instruction_Data[9]);
  Multiplexer #(.enable("false")) multiplexer_23 (
    .in0(Instruction_Data[9]), .in1(not_22_out), .out(multiplexer_23_out), .sel(OpCode[3]));

  // Other names for the same wires on the sheet: B0 = in_2[0]; B1 = in_2[1]; B2 = in_2[2]; B3 = in_2[3]; B4 = in_2[4];
  //   B5 = in_2[5]; B6 = in_2[6]; B7 = in_2[7]; B8 = in_2[8]; B9 = in_2[9]; i0 = Instruction_Data[0];
  //   MOVI[9:0] = Instruction_Data; i1 = Instruction_Data[1]; i2 = Instruction_Data[2]; i3 = Instruction_Data[3];
  //   i4 = Instruction_Data[4]; i5 = Instruction_Data[5]; i6 = Instruction_Data[6]; i7 = Instruction_Data[7];
  //   i8 = Instruction_Data[8]; i9 = Instruction_Data[9]; A0 = in_1[0]; MOV[9:0] = in_1; NOP_t[9:0] = in_1;
  //   A1 = in_1[1]; A2 = in_1[2]; A3 = in_1[3]; A4 = in_1[4]; A5 = in_1[5]; A6 = in_1[6]; A7 = in_1[7]; A8 = in_1[8];
  //   A9 = in_1[9]; add_sub_i = OpCode[3]; add_sub = OpCode[4]

  // Notes on the sheet:
  //   A
  //   B
  //   addi
  //   subi
endmodule

module Register_Bank (
  input  [9:0] Data,
  input  T_Clock,
  input  Reset,
  input  [6:0] Decoder_s_Output,
  output [9:0] out_5,
  output [9:0] out_6,
  output [9:0] out_7,
  output [9:0] out_8,
  output [9:0] out_9,
  output [9:0] out_10,
  output [9:0] out_11
);

  Registe registe_1 (
    .T_Clock(T_Clock), .Data_to_write(Data), .out_5(out_5), .Enable(Decoder_s_Output[0]));  // open: Reset
  Registe registe_2 (
    .T_Clock(T_Clock), .Data_to_write(Data), .out_5(out_6), .Enable(Decoder_s_Output[1]));  // open: Reset
  Registe registe_3 (
    .T_Clock(T_Clock), .Data_to_write(Data), .out_5(out_7), .Enable(Decoder_s_Output[2]));  // open: Reset
  Registe registe_4 (
    .T_Clock(T_Clock), .Data_to_write(Data), .out_5(out_8), .Enable(Decoder_s_Output[3]));  // open: Reset
  Registe registe_5 (
    .T_Clock(T_Clock), .Data_to_write(Data), .out_5(out_9), .Enable(Decoder_s_Output[4]));  // open: Reset
  Registe registe_6 (
    .T_Clock(T_Clock), .Data_to_write(Data), .out_5(out_10), .Enable(Decoder_s_Output[5]));  // open: Reset
  Registe registe_7 (
    .T_Clock(T_Clock), .Data_to_write(Data), .out_5(out_11), .Enable(Decoder_s_Output[6]));  // open: Reset

  // Notes on the sheet:
  //   0
  //   1
  //   2
  //   3
  //   4
  //   5
  //   6
endmodule

module Registe (
  input  T_Clock,
  input  Enable,
  input  Reset,
  input  [9:0] Data_to_write,
  output [9:0] out_5
);

  D_Flip_Flop d_ff_1 (
    .clk(T_Clock), .D(Data_to_write[0]), .Q(out_5[0]), .en(Enable), .reset(Reset));  // open: Qn, preset
  D_Flip_Flop d_ff_2 (
    .clk(T_Clock), .D(Data_to_write[1]), .Q(out_5[1]), .en(Enable), .reset(Reset));  // open: Qn, preset
  D_Flip_Flop d_ff_3 (
    .clk(T_Clock), .D(Data_to_write[2]), .Q(out_5[2]), .en(Enable), .reset(Reset));  // open: Qn, preset
  D_Flip_Flop d_ff_4 (
    .clk(T_Clock), .D(Data_to_write[3]), .Q(out_5[3]), .en(Enable), .reset(Reset));  // open: Qn, preset
  D_Flip_Flop d_ff_5 (
    .clk(T_Clock), .D(Data_to_write[4]), .Q(out_5[4]), .en(Enable), .reset(Reset));  // open: Qn, preset
  D_Flip_Flop d_ff_6 (
    .clk(T_Clock), .D(Data_to_write[5]), .Q(out_5[5]), .en(Enable), .reset(Reset));  // open: Qn, preset
  D_Flip_Flop d_ff_7 (
    .clk(T_Clock), .D(Data_to_write[6]), .Q(out_5[6]), .en(Enable), .reset(Reset));  // open: Qn, preset
  D_Flip_Flop d_ff_8 (
    .clk(T_Clock), .D(Data_to_write[7]), .Q(out_5[7]), .en(Enable), .reset(Reset));  // open: Qn, preset
  D_Flip_Flop d_ff_9 (
    .clk(T_Clock), .D(Data_to_write[8]), .Q(out_5[8]), .en(Enable), .reset(Reset));  // open: Qn, preset
  D_Flip_Flop d_ff_10 (
    .clk(T_Clock), .D(Data_to_write[9]), .Q(out_5[9]), .en(Enable), .reset(Reset));  // open: Qn, preset
endmodule
