// Logisim project bits.circ as structural Verilog: 1 circuit, main circuit main
module main (
  input  in_1
);

  wire _1_s, _2_s, _4_s, x1, x2, x3, x4, x5, x6;
  wire [3:3] bitadder_1_out;

  BitAdder bitadder_1 (.in0({{2{in_1}}, x1, x2, x3, x4, x5, x6}), .out({bitadder_1_out[3], _4_s, _2_s, _1_s}));
  // Probe on {bitadder_1_out[3], _4_s, _2_s, _1_s}

  // Notes on the sheet:
  //   3 inputs/ full adder
  //   2 full adder -> 6 inputs: x(1-6)
  //   bit adder
  //   bits.circ
endmodule
