// Logisim project fourClockFSM.circ as structural Verilog: 1 circuit, main circuit main
module main (
);

  wire and_1_out, and_2_out, and_3_out, and_4_out, and_5_out, and_6_out, and_7_out, and_8_out, and_9_out,
       and_10_out, clock_1_out, clock_2_out, clock_3_out, d_ff_1_q, d_ff_1_qn, d_ff_2_q, d_ff_2_qn, d_ff_3_q,
       d_ff_3_qn, Go, not_1_out, not_2_out, or_1_out, or_2_out, or_3_out, t_ff_1_q, t_ff_2_q, x, z;
  wire [1:0] counter_2_q;
  wire [4:0] counter_1_q;

  not not_1 (not_1_out, x);
  and and_1 (and_1_out, d_ff_1_qn, not_1_out, d_ff_3_q);
  and and_2 (and_2_out, d_ff_1_qn, d_ff_3_q, d_ff_2_q);
  and and_3 (and_3_out, d_ff_2_qn, d_ff_1_q, d_ff_3_qn);
  and and_4 (and_4_out, d_ff_1_qn, d_ff_3_qn, d_ff_2_q);
  and and_5 (and_5_out, d_ff_1_qn, not_1_out, d_ff_2_q);
  and and_6 (and_6_out, d_ff_1_qn, d_ff_3_q, x, d_ff_2_q, d_ff_2_qn);
  and and_7 (and_7_out, d_ff_1_qn, x);
  and and_8 (and_8_out, d_ff_1_qn, d_ff_3_qn, d_ff_2_q);
  and and_9 (and_9_out, d_ff_1_q, d_ff_3_qn, d_ff_2_qn);
  and and_10 (and_10_out, d_ff_1_qn, not_1_out, d_ff_3_qn);
  // AND_Gate and_11 has open pins: in1=d_ff_1_q, in2=d_ff_3_qn, in3=d_ff_2_qn, in4=x, out=open
  Clock clock_1 (.out(clock_1_out));
  or or_1 (or_1_out, and_1_out, and_2_out, and_3_out);
  or or_2 (or_2_out, and_4_out, and_10_out, and_5_out, and_6_out);
  or or_3 (or_3_out, and_7_out, and_8_out, and_9_out);
  D_Flip_Flop d_ff_1 (.clk(clock_1_out), .D(or_1_out), .Q(d_ff_1_q), .Qn(d_ff_1_qn));  // open: preset, en, reset
  D_Flip_Flop d_ff_2 (.clk(clock_1_out), .D(or_2_out), .Q(d_ff_2_q), .Qn(d_ff_2_qn));  // open: preset, en, reset
  not not_2 (not_2_out, clock_1_out);
  D_Flip_Flop d_ff_3 (.clk(clock_1_out), .D(or_3_out), .Q(d_ff_3_q), .Qn(d_ff_3_qn));  // open: preset, en, reset
  and and_12 (z, d_ff_1_q, d_ff_2_qn, d_ff_3_qn, not_1_out, not_2_out);
  Clock clock_2 (.out(clock_2_out));
  // Probe on counter_1_q
  Counter #(.width(5), .max('h1f), .ongoal("stay")) counter_1 (
    .Q(counter_1_q), .clk(t_ff_2_q));  // open: load, D, count, carry, clr
  Clock clock_3 (.out(clock_3_out));
  TTY #(.rows(16), .cols(4)) tty_1 (.data({6'b011000, z}), .clk(clock_2_out), .we(Go));  // open: clr
  Counter #(.width(2), .max('h3)) counter_2 (.Q(counter_2_q), .clk(clock_2_out));  // open: load, D, count, carry, clr
  T_Flip_Flop t_ff_1 (.clk(clock_3_out), .T(1'b1), .Q(t_ff_1_q));  // open: Qn, preset, reset, en
  TTY #(.rows(16), .cols(4)) tty_2 (.data({6'b011000, x}), .clk(clock_2_out), .we(Go));  // open: clr
  // Probe on x
  Multiplexer #(.select(2)) multiplexer_1 (
    .in0(counter_1_q[3]), .in1(counter_1_q[2]), .in2(counter_1_q[1]), .in3(counter_1_q[0]), .out(x),
    .sel(counter_2_q));  // open: en
  not not_3 (Go, counter_1_q[4]);
  T_Flip_Flop t_ff_2 (.clk(t_ff_1_q), .T(1'b1), .Q(t_ff_2_q));  // open: Qn, preset, reset, en

  // Notes on the sheet:
  //   z
  //   Ctrl-r, then Ctrl-k.  Last line may be anything.
  //   x
  //   0000
  //   0000
  //   0000
  //   0000
  //   0000
  //   0000
  //   0000
  //   0000
  //   0000
  //   0001
  //   0000
  //   0001
  //   0000
  //   0000
  //   0000
  //   ????
endmodule
