// Logisim project overlapSOP.circ as structural Verilog: 1 circuit, main circuit main
module main (
);

  wire AD_out, BD_out, f1, f2, nABC_nD_out, nABC_out, nAD_out, nBD_out, not_1_out, not_2_out, not_3_out, X1,
       X2, X3, X4;

  not not_1 (not_1_out, X1);
  not not_2 (not_2_out, X2);
  not not_3 (not_3_out, X4);
  and nAD (nAD_out, not_1_out, X4);
  and BD (BD_out, X2, X4);
  and nABC (nABC_out, not_1_out, X2, X3);
  and AD (AD_out, X1, X4);
  and nBD (nBD_out, not_2_out, X4);
  and nABC_nD (nABC_nD_out, not_1_out, X2, X3, not_3_out);
  or or_1 (f1, nAD_out, BD_out, nABC_out);
  or or_2 (f2, AD_out, nBD_out, nABC_nD_out);

  // Notes on the sheet:
  //   A
  //   B
  //   C
  //   D
  //   ~D
  //   ~A
  //   ~B
  //   multi.circ
endmodule
