// Logisim project secded.circ as structural Verilog: 1 circuit, main circuit main
module main (
);

  wire C0, C1, C2, C3, C5, CLK, clock_1_out, E, go, not_7_out, odd_parity_1_out, odd_parity_2_out,
       odd_parity_3_out, odd_parity_4_out, reset, Z0, Z1, Z2, Z3, Z4, Z5, Z6, Z7, Z8, Z9;
  wire [1:0] _1_Flip;
  wire [2:2] _2_Flip;
  wire [3:0] multiplexer_2_out, xor_1_out;
  wire [3:3] _3_Flip;
  wire [4:4] _4_Flip;
  wire [5:0] counter_1_q;
  wire [5:5] _5_Flip;
  wire [6:6] _6_Flip;
  wire [7:7] _7_Flip;
  wire [8:8] _8_Flip;
  wire [9:0] _0_Flip, undriven;
  wire [9:9] _9_Flip;

  not not_1 (_0_Flip[0], _1_Flip[0]);
  not not_2 (_1_Flip[1], _0_Flip[1]);
  not not_3 (_2_Flip[2], _0_Flip[2]);
  not not_4 (_3_Flip[3], _0_Flip[3]);
  not not_5 (_4_Flip[4], _0_Flip[4]);
  not not_6 (_5_Flip[5], _0_Flip[5]);
  xor odd_parity_1 (odd_parity_1_out, _1_Flip[0], _0_Flip[1], _0_Flip[3], _0_Flip[4], _0_Flip[6], _0_Flip[8]);
  xor odd_parity_2 (odd_parity_2_out, _1_Flip[0], _0_Flip[2], _0_Flip[3], _0_Flip[5], _0_Flip[6], _0_Flip[9]);
  xor odd_parity_3 (odd_parity_3_out, _0_Flip[1], _0_Flip[2], _0_Flip[3], _0_Flip[7], _0_Flip[8], _0_Flip[9]);
  xor odd_parity_4 (odd_parity_4_out, _0_Flip[4], _0_Flip[5], _0_Flip[6], _0_Flip[7], _0_Flip[8], _0_Flip[9]);
  xor xor_1 (xor_1_out[0], C0, odd_parity_1_out);
  xor xor_2 (xor_1_out[1], C1, odd_parity_2_out);
  xor xor_3 (xor_1_out[2], C2, odd_parity_3_out);
  xor xor_4 (xor_1_out[3], odd_parity_4_out, C3);
  not not_7 (not_7_out, xor_1_out[2]);
  and and_1 (E, C0, xor_1_out[1], not_7_out, xor_1_out[3]);
  not not_8 (_6_Flip[6], _0_Flip[6]);
  not not_9 (_7_Flip[7], _0_Flip[7]);
  not not_10 (_8_Flip[8], _0_Flip[8]);
  not not_11 (_9_Flip[9], _0_Flip[9]);
  Multiplexer #(.select(4), .width(10), .enable("false")) multiplexer_1 (
    .in0({_0_Flip[9:1], _1_Flip[0]}), .in1({_0_Flip[9:1], _1_Flip[0]}), .in2({_0_Flip[9:1], _1_Flip[0]}),
    .in3(_0_Flip), .in4(undriven), .in5({_0_Flip[9:2], _1_Flip}),
    .in6({_0_Flip[9:3], _2_Flip[2], _0_Flip[1], _1_Flip[0]}),
    .in7({_0_Flip[9:4], _3_Flip[3], _0_Flip[2:1], _1_Flip[0]}), .in8({_0_Flip[9:1], _1_Flip[0]}),
    .in9({_0_Flip[9:5], _4_Flip[4], _0_Flip[3:1], _1_Flip[0]}),
    .in10({_0_Flip[9:6], _5_Flip[5], _0_Flip[4:1], _1_Flip[0]}),
    .in11({_0_Flip[9:7], _6_Flip[6], _0_Flip[5:1], _1_Flip[0]}),
    .in12({_0_Flip[9:8], _7_Flip[7], _0_Flip[6:1], _1_Flip[0]}), .in13({_0_Flip[9:1], _1_Flip[0]}),
    .in14({_0_Flip[9], _8_Flip[8], _0_Flip[7:1], _1_Flip[0]}), .in15({_9_Flip[9], _0_Flip[8:1], _1_Flip[0]}),
    .out({Z9, Z8, Z7, Z6, Z5, Z4, Z3, Z2, Z1, Z0}), .sel(xor_1_out));
  // Probe on {1'b0, E, Z9, Z8}
  Counter #(.width(6), .max('h33), .ongoal("stay")) counter_1 (
    .Q(counter_1_q), .clk(CLK), .clr(reset));  // open: load, D, count, carry
  // Probe on {Z7, Z6, Z5, Z4}
  Multiplexer #(.select(2), .width(4), .disabled(0)) multiplexer_2 (
    .in0(4'b0000), .in1({1'b0, E, Z9, Z8}), .in2({Z7, Z6, Z5, Z4}), .in3({Z3, Z2, Z1, Z0}),
    .out(multiplexer_2_out), .sel(counter_1_q[1:0]));  // open: en
  not not_12 (go, counter_1_q[5]);
  Clock clock_1 (.out(clock_1_out));
  // Probe on {Z3, Z2, Z1, Z0}
  and and_2 (CLK, go, clock_1_out);
  TTY #(.cols(4)) tty_1 (.data({3'b100, multiplexer_2_out}), .clk(CLK), .we(go), .clr(reset));
  ROM #(.addrWidth(3), .dataWidth(15)) rom_1 (
    .addr(counter_1_q[4:2]), .data({C5, _0_Flip[9:4], C3, _0_Flip[3:1], C2, _1_Flip[0], C1, C0}));  // open: sel
  Button u_Reset (.out(reset));
  // Probe on {C5, _0_Flip[9:4], C3, _0_Flip[3:1], C2, _1_Flip[0], C1, C0}

  // Other names for the same wires on the sheet: _2_Flip (some bits) = {_0_Flip[9:3], _0_Flip[1], _1_Flip[0]};
  //   _3_Flip (some bits) = {_0_Flip[9:4], _0_Flip[2:1], _1_Flip[0]};
  //   _4_Flip (some bits) = {_0_Flip[9:5], _0_Flip[3:1], _1_Flip[0]};
  //   _5_Flip (some bits) = {_0_Flip[9:6], _0_Flip[4:1], _1_Flip[0]};
  //   _6_Flip (some bits) = {_0_Flip[9:7], _0_Flip[5:1], _1_Flip[0]};
  //   _7_Flip (some bits) = {_0_Flip[9:8], _0_Flip[6:1], _1_Flip[0]};
  //   _8_Flip (some bits) = {_0_Flip[9], _0_Flip[7:1], _1_Flip[0]}; _9_Flip[8:0] = {_0_Flip[8:1], _1_Flip[0]};
  //   D0 = _1_Flip[0]; G[9:0] = {_0_Flip[9:1], _1_Flip[0]}; D1 = _0_Flip[1]; _1_Flip[9:2] = _0_Flip[9:2];
  //   D2 = _0_Flip[2]; D3 = _0_Flip[3]; D4 = _0_Flip[4]; D5 = _0_Flip[5]; D6 = _0_Flip[6]; D7 = _0_Flip[7];
  //   D8 = _0_Flip[8]; D9 = _0_Flip[9]

  // Notes on the sheet:
  //   Press Reset and Ctrl-T or Ctrl-K
  //   Please set tick frequency to 2KHz
  //   @CJA
  //   @GFK
  //   contents of rom_1 (hex, n*v repeats v):
  //   4e90 49c0 68d3 7a0c d5f 3457 3d95 4154
  //   @@NB
  //   @@KH
  //   @FLJ
  //   @@MK
  //   @CMC
  //   @@AK
endmodule
